# Fritzing sketch cloudScaleSchematic (saved by Fritzing 0.9.2b)

parts:
  U1 = LIPO-110mAh [package=lipo-110]
  BAT1 = Battery Holders [package=battcom_20mm_pth]
  LCD1 = LCD screen
  Part3 = Arduino Pro Mini v13
  U4 = ESP8266 WiFi Module [part_number=ESP8266]
  Part4 = Power Cell LiPo Charger/Booster
  part = LCD screen  # not connected
  JP1 = Header 6 [package=molex-1x6_lock]

nets:
  N1: U1.+, Part4.VBATT
  GND: U1.-, LCD1.V0, Part3.GND, U4.GND, Part4.GND, JP1.1, JP1.3
  N2: BAT1.+, LCD1.VDD
  N3: LCD1.E, Part4.EN
  N4: LCD1.DB2, Part3.A5
  N5: LCD1.DB3, Part3.A4
  N6: LCD1.DB4, Part3.A3
  N7: LCD1.DB5, Part3.A2
  N8: LCD1.DB6, Part3.A1
  N9: LCD1.DB7, Part3.A0, Part3.D13/SCK
  N10: Part3.DTR, JP1.6
  N11: Part3.D0/TX, JP1.5
  VCC: Part3.D1/RX, Part3.VCC, U4.VCC, U4.CH_PD, Part4.VCC, JP1.2, JP1.4
  N12: Part3.D7, Part3.D6_PWM, U4.RST
  N13: Part3.D5_PWM, U4.GPIO_0
  N14: Part3.D4, Part3.D3_PWM, U4.TXD
  N15: Part3.D2, U4.RXD

custom parts:
  ESP8266 WiFi Module: Generic WiFi Module based on the ESP8266 with onboard PCB antenna and UART communications
